# Fritzing sketch airsoft-domination-onebutton-schematic (saved by Fritzing 0.9.3b)
breadboards: 1

parts:
  S1 = Pushbutton [package="[THT]"]
  R1 = Resistor [tolerance=±5% resistance=10k package=THT]
  SG1 = Buzzer 12mm [package=buzzer-12mm-ns]
  C1 = Capacitor Polarized [package=nippon_f80]
  Part2 = Lithium Ion Polymer Battery 3.7v 1200mAh [part_number=258]
  NEOPIXEL1 = Neopixel Strip -- Black (60/m)
  Part3 = Adafruit Trinket 5V

nets:
  N1: S1.Pin_1, S1.Pin_2, C1.+, Part2.positive, NEOPIXEL1.+5V, Part3.VBAT
  N2: S1.Pin_3, S1.Pin_4, R1.Pin_1, Part3.#2
  GND: R1.Pin_0, SG1.2, C1.-, Part2.negative, NEOPIXEL1.GND, Part3.GND
  N3: SG1.1, Part3.#1
  N4: NEOPIXEL1.DI, Part3.#0

custom parts:
  Lithium Ion Polymer Battery 3.7v 1200mAh: Lithium ion polymer (also known as 'lipo' or 'lipoly') batteries are thin, light and powerful. The output ranges from 4.2V when completely charged to 3.7V. This battery has a capacity of 1200mAh for a total of about 4.5 Wh. The batteries come pre-attached with a genuine 2-pin JST-PH connector as shown and include the necessary protection circuitry.
  Neopixel Strip -- Black (60/m): Neopixel Strip, Black, 60 pixels per meter.
  Adafruit Trinket 5V: Trinket may be small, but do not be fooled by its size! It's a tiny microcontroller board, built around the Atmel ATtiny85, a little chip with a lot of power. We wanted to design a microcontroller board that was small enough to fit into any project, and low cost enough to use without hesitation. Perfect for when you don't want to give up your expensive dev-board and you aren't willing to take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
